// Logisim project trabalho_cc.circ as structural Verilog
module Contador (
  input  in_1
);

  wire and_1_out, and_2_out, and_3_out, and_4_out, and_5_out, and_6_out, and_7_out, and_8_out, and_9_out,
       and_10_out, and_11_out, and_12_out, and_13_out, and_14_out, and_15_out, and_16_out, and_17_out,
       and_18_out, and_19_out, and_20_out, and_21_out, d_ff_1_q, d_ff_1_qn, d_ff_2_q, d_ff_2_qn, d_ff_3_q,
       d_ff_3_qn, or_1_out, or_2_out, or_3_out, or_4_out, or_5_out, or_6_out, or_7_out, or_8_out, or_9_out,
       or_10_out, or_11_out;

  D_Flip_Flop d_ff_1 (.D(or_9_out), .clk(in_1), .Q(d_ff_1_q), .Qn(d_ff_1_qn));  // open: preset, reset
  D_Flip_Flop d_ff_2 (.D(or_10_out), .clk(in_1), .Q(d_ff_2_q), .Qn(d_ff_2_qn));  // open: preset, reset
  D_Flip_Flop d_ff_3 (.D(or_11_out), .clk(in_1), .Q(d_ff_3_q), .Qn(d_ff_3_qn));  // open: preset, reset
  and and_1 (and_1_out, d_ff_1_qn, d_ff_2_q, d_ff_3_q);
  and and_2 (and_2_out, d_ff_1_q, d_ff_2_qn, d_ff_3_qn);
  and and_3 (and_3_out, d_ff_1_qn, d_ff_2_qn, d_ff_3_q);
  and and_4 (and_4_out, d_ff_1_qn, d_ff_2_q, d_ff_3_qn);
  and and_5 (and_5_out, d_ff_1_qn, d_ff_2_qn, d_ff_3_qn);
  and and_6 (and_6_out, d_ff_1_qn, d_ff_2_q, d_ff_3_qn);
  and and_7 (and_7_out, d_ff_1_q, d_ff_2_qn, d_ff_3_qn);
  or or_1 (or_1_out, d_ff_1_qn, d_ff_2_q, d_ff_3_q);
  or or_2 (or_2_out, d_ff_1_qn, d_ff_2_q, d_ff_3_qn);
  and and_8 (and_8_out, d_ff_1_q, d_ff_2_qn, d_ff_3_q);
  and and_9 (and_9_out, d_ff_1_q, d_ff_2_qn, d_ff_3_qn);
  or or_3 (or_3_out, d_ff_1_q, d_ff_2_q, d_ff_3_qn);
  or or_4 (or_4_out, d_ff_1_q, d_ff_2_qn, d_ff_3_q);
  and and_10 (and_10_out, d_ff_1_qn, d_ff_2_q, d_ff_3_qn);
  and and_11 (and_11_out, d_ff_1_qn, d_ff_2_qn, d_ff_3_q);
  or or_5 (or_5_out, d_ff_1_qn, d_ff_2_q, d_ff_3_q);
  or or_6 (or_6_out, d_ff_1_qn, d_ff_2_q, d_ff_3_qn);
  and and_12 (and_12_out, d_ff_1_q, d_ff_2_qn, d_ff_3_q);
  and and_13 (and_13_out, d_ff_1_q, d_ff_2_qn, d_ff_3_qn);
  or or_7 (or_7_out, d_ff_1_q, d_ff_2_q, d_ff_3_qn);
  or or_8 (or_8_out, d_ff_1_q, d_ff_2_qn, d_ff_3_q);
  and and_14 (and_14_out, d_ff_1_qn, d_ff_2_q, d_ff_3_qn);
  and and_15 (and_15_out, d_ff_1_qn, d_ff_2_qn, d_ff_3_q);
  and and_16 (and_16_out, d_ff_1_qn, d_ff_2_qn, d_ff_3_q);
  and and_17 (and_17_out, d_ff_1_qn, d_ff_2_q, d_ff_3_qn);
  or or_9 (or_9_out, and_1_out, and_2_out);
  or or_10 (or_10_out, and_3_out, and_4_out);
  or or_11 (or_11_out, and_5_out, and_6_out, and_7_out);
  and and_18 (and_18_out, or_1_out, or_2_out);
  and and_19 (and_19_out, or_3_out, or_4_out);
  and and_20 (and_20_out, or_5_out, or_6_out);
  and and_21 (and_21_out, or_7_out, or_8_out);
  LED led_1 (.in(and_16_out));
  LED led_2 (.in(and_17_out));
  LED led_3 (.in(and_18_out));
  LED led_4 (.in(and_8_out));
  LED led_5 (.in(and_9_out));
  LED led_6 (.in(and_19_out));
  LED led_7 (.in(and_10_out));
  LED led_8 (.in(and_11_out));
  LED led_9 (.in(and_20_out));
  LED led_10 (.in(and_12_out));
  LED led_11 (.in(and_13_out));
  LED led_12 (.in(and_21_out));
  LED led_13 (.in(and_14_out));
  LED led_14 (.in(and_15_out));

  // Notes on the sheet:
  //   Farol 1
  //   Farol 2
  //   Farol 3
  //   Farol 4
  //   Pedestre
endmodule
